# Fritzing sketch CatFeedingInfo_Nano (saved by Fritzing 0.9.2b)
circuit board: 6cm x 4cm
breadboards: 1

parts:
  LCD1 = LCD screen
  LED1 = LED - 5mm [color="Red (633nm)" package="5 mm [THT]"]
  LED2 = LED - 5mm [color="Yellow (595nm)" package="5 mm [THT]"]
  LED3 = LED - 5mm [color="Green (565nm)" package="5 mm [THT]"]
  S1 = Pushbutton [package="[THT]"]
  S2 = Pushbutton [package="[THT]"]
  Q1 = NPN-Transistor [package="TO92 [THT]"]
  R2 = Resistor [tolerance=±5% resistance=220 package=THT]
  R3 = Resistor [tolerance=±5% resistance=220 package=THT]
  R4 = Resistor [tolerance=±5% resistance=220 package=THT]
  Arduino_Nano = Arduino Nano (Rev3.0)
  R1 = Resistor [tolerance=±5% resistance=220 package=THT]

nets:
  VSS: LCD1.VSS, LCD1.VDD, LCD1.V0, LCD1.R/W, S1.Pin_1, S1.Pin_2, S2.Pin_3, S2.Pin_4, R2.Pin_1, R3.Pin_1, R4.Pin_1
  N1: LCD1.DB4, Arduino_Nano.A3
  N2: LCD1.DB5, Arduino_Nano.A4
  N3: LCD1.DB6, Arduino_Nano.A5
  N4: LCD1.DB7, Arduino_Nano.A6
  N5: LCD1.LED+, R1.Pin_0
  N6: LCD1.LED-, Q1.C
  N7: LED1.cathode, R2.Pin_0
  N8: LED1.anode, Arduino_Nano.D10
  N9: LED2.cathode, R3.Pin_0
  N10: LED2.anode, Arduino_Nano.D11/MOSI
  N11: LED3.cathode, R4.Pin_0
  N12: LED3.anode, Arduino_Nano.D12/MISO
  N13: S1.Pin_3, S1.Pin_4, Arduino_Nano.D3
  N14: S2.Pin_1, S2.Pin_2, Arduino_Nano.D2
  N15: Q1.E, Arduino_Nano.GND
  N16: Q1.B, Arduino_Nano.A7
  N17: Arduino_Nano.5V, R1.Pin_1

notes:
  Buttons use internal pull-up resistors. Note that the logic is inverted from original schematic
